# Fritzing sketch Gizmo_board2 (saved by Fritzing 0.9.3b)
circuit board: 6.86cm x 5.35cm

parts:
  ARDUINO = Arduino Nano (Rev3.0)
  SWITCH = SPST Switch [package=switch-spdt_kit]
  IR_RECEIVE2 = LED - 5mm [color="Blue (430nm)" package="5 mm [THT]"]
  IR_RECEIVE1 = LED - 5mm [color="Blue (430nm)" package="5 mm [THT]"]
  IR_EMIT1 = LED - 5mm [color="Infrared (940nm)" package="5 mm [THT]"]
  R1 = Resistor [tolerance=±5% resistance=180 package="0805 [SMD]"]
  R2 = Resistor [tolerance=±5% resistance=180 package="0805 [SMD]"]
  180 = Resistor [tolerance=±5% resistance=100 package="0805 [SMD]"]
  180_2 = Resistor [tolerance=±5% resistance=100 package="0805 [SMD]"]
  47K = Resistor [tolerance=±5% resistance=47k package="0805 [SMD]"]
  BLUETOOTH = Bluetooth HC-05 Macho
  RGB_LED = Header 4 [package=molex-1x4_lock]
  ULTRA_DIST = Header 4 [package=molex-1x4_lock]
  V_MOTOR = Header 2 [package=screwterminal-3.5mm-2_lock]
  74HC139N2 = 74HC139N [part_number=74HC139N package="DIP (Dual Inline) [THT]"]
  R3 = Resistor [tolerance=±5% resistance=180 package="0805 [SMD]"]
  SERVO_ARM = Dagu DGServo 9g header (male) [package=THT]
  V_BATT = Header 2 [package=screwterminal-3.5mm-2_lock]
  ULN2803A = ULN2803A [package=THT]
  STEPPER1 = male pin header, 5 pins [form="♂ (male)"]
  STEPPER2 = male pin header, 5 pins [form="♂ (male)"]
  IR_EMIT2 = LED - 5mm [color="Infrared (940nm)" package="5 mm [THT]"]
  47K_2 = Resistor [tolerance=±0.05% resistance=47k package="0805 [SMD]"]

nets:
  N1: ARDUINO.D1/TX, BLUETOOTH.TXD
  N2: ARDUINO.D0/RX, BLUETOOTH.RXD
  GND: ARDUINO.GND, IR_RECEIVE2.anode, IR_RECEIVE1.anode, IR_EMIT1.cathode, BLUETOOTH.GND, ULTRA_DIST.4, V_MOTOR.2, 74HC139N2.GND, SERVO_ARM.gnd, V_BATT.2, ULN2803A.0V, IR_EMIT2.cathode
  N3: ARDUINO.D2, ULTRA_DIST.2
  N4: ARDUINO.D3, ULTRA_DIST.3
  N5: ARDUINO.D4, 74HC139N2.2A
  N6: ARDUINO.D5, 74HC139N2.2B
  N7: ARDUINO.D6, SERVO_ARM.pulse
  N8: ARDUINO.D7, 74HC139N2.1A
  N9: ARDUINO.D8, 74HC139N2.1B
  N10: ARDUINO.D9, R3.Pin_0
  N11: ARDUINO.D10, R2.Pin_0
  N12: ARDUINO.D11/MOSI, R1.Pin_0
  N13: ARDUINO.D12/MISO, 74HC139N2.1G_, 74HC139N2.2G_
  N14: ARDUINO.VIN, SWITCH.P
  VCC: ARDUINO.5V, IR_RECEIVE2.cathode, IR_RECEIVE1.cathode, 180.Pin_1, 180_2.Pin_1, 47K.Pin_0, BLUETOOTH.VCC, RGB_LED.2, ULTRA_DIST.1, 74HC139N2.VCC, 47K_2.Pin_0
  N15: ARDUINO.A1, 47K.Pin_1
  N16: ARDUINO.A0, 47K_2.Pin_1
  N17: SWITCH.O, V_BATT.1
  N18: IR_EMIT1.anode, 180.Pin_0
  N19: R1.Pin_1, RGB_LED.4
  N20: R2.Pin_1, RGB_LED.3
  N21: 180_2.Pin_0, IR_EMIT2.anode
  N22: RGB_LED.1, R3.Pin_1
  N23: V_MOTOR.1, SERVO_ARM.Vcc, ULN2803A.COM_-_Common, STEPPER1.pin3, STEPPER2.pin3
  N24: 74HC139N2.1Y0, ULN2803A.In_1
  N25: 74HC139N2.1Y1, ULN2803A.In_2
  N26: 74HC139N2.1Y2, ULN2803A.In_3
  N27: 74HC139N2.1Y3, ULN2803A.In_4
  N28: 74HC139N2.2Y3, ULN2803A.In_8
  N29: 74HC139N2.2Y2, ULN2803A.In_7
  N30: 74HC139N2.2Y1, ULN2803A.In_6
  N31: 74HC139N2.2Y0, ULN2803A.In_5
  N32: ULN2803A.Out_8, STEPPER2.pin5
  N33: ULN2803A.Out_7, STEPPER2.pin4
  N34: ULN2803A.Out_6, STEPPER2.pin2
  N35: ULN2803A.Out_5, STEPPER2.pin1
  N36: ULN2803A.Out_4, STEPPER1.pin5
  N37: ULN2803A.Out_3, STEPPER1.pin4
  N38: ULN2803A.Out_2, STEPPER1.pin2
  N39: ULN2803A.Out_1, STEPPER1.pin1

notes:
  Do not connect red wires on stepper motors
